// Logisim project design.circ as structural Verilog: 6 circuits, main circuit main
module main (
  input  in_1,
  output [15:0] out_2
);

  wire AC_out, analizadorteclado_1_out_4, button_out, clock_1_out, or_1_out, or_2_out;
  wire [6:0] analizadorteclado_1_salida_ascii, analizadorteclado_1_salida_binario;
  wire [18:0] _1_out;

  Clock clock_1 (.out(clock_1_out));
  or or_1 (or_1_out, clock_1_out, analizadorteclado_1_out_4);
  AnalizadorTeclado analizadorteclado_1 (
    .Entrada({_1_out[18:11], in_1, _1_out[9:0]}), .Salida_ASCII(analizadorteclado_1_salida_ascii),
    .Salida_binario(analizadorteclado_1_salida_binario), .out_4(analizadorteclado_1_out_4));
  TTY #(.rows(1), .cols(30)) tty_1 (
    .data(analizadorteclado_1_salida_ascii), .clk(analizadorteclado_1_out_4), .clr(or_2_out));  // open: we
  or or_2 (or_2_out, button_out, AC_out);
  Button _2 (.out(_1_out[1]));
  Button _1 (.out(_1_out[0]));
  Button _4 (.out(_1_out[3]));
  Button _5 (.out(_1_out[4]));
  Button _8 (.out(_1_out[7]));
  Button _7 (.out(_1_out[6]));
  Button _0 (.out(_1_out[9]));
  Button AC (.out(AC_out));
  MemoriaInstrucciones memoriainstrucciones_1 (
    .Entrada(analizadorteclado_1_salida_binario), .Reloj(or_1_out), .Reset_mem(AC_out),
    ._0_leer_1_escribir(button_out), .Salida(out_2));
  Button _3 (.out(_1_out[2]));
  Button _6 (.out(_1_out[5]));
  Button _9 (.out(_1_out[8]));
  Button button (.out(button_out));
  Button button_2 (.out(_1_out[14]));
  Button button_3 (.out(_1_out[18]));
  Button button_4 (.out(_1_out[17]));
  Button button_5 (.out(_1_out[13]));
  Button button_6 (.out(_1_out[16]));
  Button x (.out(_1_out[12]));
  Button button_7 (.out(_1_out[11]));
  Button x_y (.out(_1_out[15]));
endmodule

module AnalizadorTeclado (
  input  [18:0] Entrada,
  output [6:0] Salida_ASCII,
  output [6:0] Salida_binario,
  output out_4
);

  ROM #(.addrWidth(19), .dataWidth(7), .Select("low")) rom_1 (.addr(Entrada), .data(Salida_ASCII));
  ROM #(.addrWidth(19), .dataWidth(7), .Select("low")) rom_2 (.addr(Entrada), .data(Salida_binario));
  or or_1 (out_4, Salida_ASCII[0], Salida_ASCII[1], Salida_ASCII[2], Salida_ASCII[3], Salida_ASCII[4], Salida_ASCII[5], Salida_ASCII[6]);

  // Notes on the sheet:
  //   contents of rom_1 (hex, n*v repeats v):
  //   0 31 32 0 33 0 0 0 34 7*0 35 15*0 36 31*0 37 63*0 38 127*0 39 255*0 30 511*0 3d 1023*0 21 2047*0 2a
  //   4095*0 2b 8191*0 28 16383*0 5e 32767*0 25 65535*0 2d 131071*0 29
  //   contents of rom_2 (hex, n*v repeats v):
  //   0 1 2 0 3 0 0 0 4 7*0 5 15*0 6 31*0 7 63*0 8 127*0 9 767*0 3d 1023*0 21 2047*0 2a 4095*0 2b 8191*0
  //   28 16383*0 5e 32767*0 25 65535*0 2d 131071*0 29
endmodule

module Potenciador (
  input  [15:0] Base,
  input  [15:0] Exponente,
  input  Reloj,
  output [15:0] Salida
);

  wire comparator_1_eq, comparator_2_eq, not_1_out, register_3_q;
  wire [15:0] counter_1_q, multiplexer_1_out, multiplier_1_out, register_1_q, register_2_q;

  Multiplexer #(.width(16), .enable("false")) multiplexer_1 (
    .in0(Base), .in1(multiplier_1_out), .out(multiplexer_1_out), .sel(not_1_out));
  not not_1 (not_1_out, comparator_2_eq);
  Register #(.width(16), .Select("low")) register_1 (.D(Exponente), .Q(register_1_q), .clk(Reloj));  // open: en, clr
  Counter #(.width(16), .max('hffff)) counter_1 (
    .Q(counter_1_q), .clk(Reloj), .clr(register_3_q));  // open: load, D, count, carry, preset, down
  Register #(.width(16), .Select("low")) register_2 (
    .D(multiplexer_1_out), .Q(register_2_q), .clk(Reloj));  // open: en, clr
  Comparator #(.width(16)) comparator_1 (.a(register_1_q), .b(counter_1_q), .eq(comparator_1_eq));  // open: gt, lt
  Comparator #(.width(16)) comparator_2 (.a(counter_1_q), .b({16{1'b0}}), .eq(comparator_2_eq));  // open: gt, lt
  Multiplier #(.width(16)) multiplier_1 (.a(register_2_q), .b(Base), .out(multiplier_1_out));  // open: cin, cout
  Register #(.width(1), .Select("low")) register_3 (
    .D(comparator_1_eq), .Q(register_3_q), .clk(Reloj));  // open: en, clr
  Register #(.width(16), .Select("low")) register_4 (
    .D(register_2_q), .en(comparator_1_eq), .Q(Salida), .clk(Reloj));  // open: clr

  // Notes on the sheet:
  //   Contador
endmodule

module MemoriaInstrucciones (
  input  [6:0] Entrada,
  input  Reloj,
  input  Reset_mem,
  input  _0_leer_1_escribir,
  output [15:0] Salida
);

  wire decodificadordeinstrucciones_1_disablepc, t_ff_1_q, t_ff_1_qn;
  wire [6:0] counter_1_q;
  wire [15:0] controlled_buffer_1_out, decodificadordeinstrucciones_1_salida;

  Counter #(.width(7), .max('h7f)) counter_1 (
    .count(decodificadordeinstrucciones_1_disablepc), .Q(counter_1_q), .clk(Reloj), .clr(_0_leer_1_escribir));  // open: load, D, carry, preset, down
  decodificadorDeInstrucciones decodificadordeinstrucciones_1 (
    .Reloj(Reloj), .Entrada(Entrada), .DisablePC(decodificadordeinstrucciones_1_disablepc),
    .Salida(decodificadordeinstrucciones_1_salida));
  T_Flip_Flop t_ff_1 (.clk(_0_leer_1_escribir), .T(1'b1), .Q(t_ff_1_q), .Qn(t_ff_1_qn));  // open: preset, reset
  assign controlled_buffer_1_out = t_ff_1_qn ? decodificadordeinstrucciones_1_salida : 16'bz;  // Controlled_Buffer controlled_buffer_1
  RAM #(.addrWidth(7), .dataWidth(16), .Select("low")) ram_1 (
    .addr(counter_1_q), .data(controlled_buffer_1_out), .clk(Reloj), .ld(t_ff_1_q), .clr(Reset_mem));  // open: sel
  assign Salida = t_ff_1_q ? controlled_buffer_1_out : 16'bz;  // Controlled_Buffer controlled_buffer_2
endmodule

module Factorial (
  input  [15:0] Number,
  input  in_2,
  input  in_3,
  output [15:0] out_4
);

  wire comparator_1_eq, comparator_2_eq, comparator_2_gt, not_1_out, or_1_out;
  wire [15:0] counter_1_q, multiplexer_1_out, multiplier_1_out, register_1_q, register_2_q, register_4_q,
       subtractor_1_out;

  Multiplexer #(.width(16), .enable("false")) multiplexer_1 (
    .in0(multiplier_1_out), .in1(Number), .out(multiplexer_1_out), .sel(comparator_1_eq));
  Register #(.width(16), .Select("low")) register_1 (
    .D(multiplexer_1_out), .Q(register_1_q), .clk(in_2));  // open: en, clr
  Counter #(.width(16), .max('hffff)) counter_1 (
    .Q(counter_1_q), .clk(in_2), .clr(in_3));  // open: load, D, count, carry, preset, down
  Register #(.width(16), .Select("low")) register_2 (.Q(register_2_q));  // open: D, en, clk, clr
  not not_1 (not_1_out, or_1_out);
  Subtractor #(.width(16)) subtractor_1 (.a(register_4_q), .b(counter_1_q), .out(subtractor_1_out));  // open: bin, bout
  Comparator #(.width(16)) comparator_1 (.a(counter_1_q), .b(register_2_q), .eq(comparator_1_eq));  // open: gt, lt
  or or_1 (or_1_out, comparator_2_gt, comparator_2_eq);
  Register #(.width(16), .Select("low")) register_3 (
    .D(multiplier_1_out), .en(not_1_out), .Q(out_4), .clk(in_2));  // open: clr
  Multiplier #(.width(16)) multiplier_1 (
    .a(register_1_q), .b(subtractor_1_out), .out(multiplier_1_out));  // open: cin, cout
  Comparator #(.width(16)) comparator_2 (
    .a(counter_1_q), .b(register_4_q), .gt(comparator_2_gt), .eq(comparator_2_eq));  // open: lt
  Register #(.width(16), .Select("low")) register_4 (
    .D(Number), .en(comparator_1_eq), .Q(register_4_q), .clk(in_2));  // open: clr
endmodule

module decodificadorDeInstrucciones (
  input  Reloj,
  input  [6:0] Entrada,
  output DisablePC,
  output [15:0] Salida
);

  wire comparator_1_gt, comparator_1_lt, d_ff_1_qn;
  wire [15:0] bit_extender_1_out, multiplexer_1_out, multiplier_1_out, register_1_q;

  D_Flip_Flop d_ff_1 (.clk(Reloj), .D(comparator_1_gt), .Qn(d_ff_1_qn));  // open: Q, preset, reset
  Comparator #(.width(7)) comparator_1 (
    .a(Entrada), .b(7'b0001010), .gt(comparator_1_gt), .lt(comparator_1_lt));  // open: eq
  assign bit_extender_1_out = {{9{1'b0}}, Entrada};  // Bit_Extender bit_extender_1
  nand nand_1 (DisablePC, d_ff_1_qn, comparator_1_lt);
  Register #(.width(16), .Select("low")) register_1 (.D(Salida), .Q(register_1_q), .clk(Reloj));  // open: en, clr
  Multiplier #(.width(16)) multiplier_1 (.a(register_1_q), .b(16'ha), .out(multiplier_1_out));  // open: cin, cout
  Multiplexer #(.width(16), .enable("false")) multiplexer_1 (
    .in0(multiplier_1_out), .in1({16{1'b0}}), .out(multiplexer_1_out), .sel(DisablePC));
  Adder #(.width(16)) adder_1 (.a(multiplexer_1_out), .b(bit_extender_1_out), .out(Salida));  // open: cin, cout

  // Notes on the sheet:
  //   Estados:
  //   0- Número
  //   1- Operador
endmodule
